# Fritzing sketch Projet (saved by Fritzing 0.9.2b)
breadboards: 1

parts:
  Arduino_Uno = Arduino Uno (Rev3)
  U1 = L298 [package=multiwatt15_6400bgheatsink]
  M1 = DC Motor
  M2 = DC Motor
  R1 = Resistor [tolerance=±5% resistance=220 package=THT]
  LED = smd LED [color="Blue (525nm)" package="1206 [SMD]"]
  LCD = LCD1602-I2C
  IC1 = DS1302 [package="SO8 [SMD]"]

nets:
  N1: Arduino_Uno.D8, U1.IN2
  N2: Arduino_Uno.D9_PWM, U1.IN3
  N3: Arduino_Uno.D10_PWM/SS, U1.IN4
  N4: Arduino_Uno.D11_PWM/MOSI, IC1.SCLK_-_SPI_Clock
  N5: Arduino_Uno.D12/MISO, IC1.I/O_-_SPI_Data_In/Out
  N6: Arduino_Uno.D13/SCK, LED.anode
  GND: Arduino_Uno.GND, U1.GND, R1.Pin_1, LCD.GND
  N7: Arduino_Uno.D4, IC1.CE_-_Chip_Enable
  N8: Arduino_Uno.D5_PWM, U1.ENA
  N9: Arduino_Uno.D6_PWM, U1.ENB
  N10: Arduino_Uno.D7, U1.IN1
  5V: Arduino_Uno.5V, U1.VLS, LCD.VCC, IC1.+V
  N11: U1.OUT1, M1.pin_1
  N12: U1.OUT2, M1.pin_2
  12V: U1.VS
  N13: U1.OUT3, M2.pin_1
  N14: U1.OUT4, M2.pin_2
  N15: R1.Pin_0, LED.cathode

custom parts:
  LCD1602-I2C: A standard character display, usually with 2x16 characters. Comes in many colors with LCM1602 IIC attached.
