# Fritzing sketch Projet2 (saved by Fritzing 0.9.2b)

parts:
  Composant1 = Arduino Uno (Rev3)
  RE2 = Rotary Encoder [package=THT]
  R4 = Photocell (LDR) [package=THT]
  R5 = Resistor [tolerance=±20% resistance=1k package=THT]
  BT1 = Bluetooth HC-06u [package=THT]
  S1 = Square Pushbutton
  R6 = Resistor [tolerance=±5% resistance=10k package=THT]
  S2 = Square Pushbutton
  R7 = Resistor [tolerance=±5% resistance=10k package=THT]

nets:
  N1: Composant1.A0, R4.pin_0, R5.Pin_0
  N2: Composant1.A1, R6.Pin_0
  N3: Composant1.A2, S2.leg1, R7.Pin_0
  N4: Composant1.D2, RE2.EncoderPinA
  N5: Composant1.D3_PWM, RE2.EncoderPinB
  5V: Composant1.5V, R5.Pin_1, BT1.VCC, R6.Pin_1, R7.Pin_1
  N6: R4.pin_1, BT1.GND, S1.leg0, S2.leg0

custom parts:
  Bluetooth HC-06u: Bluetooth HC-06 - face up, pins down 16.5mm x 37.5mm PCB
